// Logisim project alu-control.circ as structural Verilog: 1 circuit, main circuit main
module main (
  input  [1:0] Opcode,
  input  [5:0] Funct,
  input  [1:0] sh,
  output [3:0] ALUControl
);


  // Notes on the sheet:
  //   DO NOT MOVE, CHANGE, ADD, OR REMOVE INPUTS AND OUTPUTS!!!
endmodule
