// Logisim project alu.circ as structural Verilog: 10 circuits, main circuit main
module main (
  input  [31:0] A,
  input  [31:0] B,
  input  [3:0] ALUControl,
  output [3:0] ALUFlags,
  output [31:0] Result
);

  wire AND_carryout, ASR_carryout, Difference_carryout, LSL_carryout, LSR_carryout, NOT_carryout,
       OR_carryout, Sum_carryout, XOR_carryout;
  wire [31:0] AND_result, ASR_result, Difference_result, LSL_result, LSR_result, NOT_result, OR_result,
       Sum_result, XOR_result;

  AND AND (.in_1(A), .in_2(B), .Result(AND_result), .CarryOut(AND_carryout));
  OR OR (.in_1(A), .in_2(B), .Result(OR_result), .CarryOut(OR_carryout));
  XOR XOR (.in_1(A), .in_2(B), .Result(XOR_result), .CarryOut(XOR_carryout));
  NOT NOT (.in_1(A), .Result(NOT_result), .CarryOut(NOT_carryout));
  LSL LSL (.in_1(B), .in_2(A), .Result(LSL_result), .CarryOut(LSL_carryout));
  LSR LSR (.in_1(B), .in_2(A), .Result(LSR_result), .CarryOut(LSR_carryout));
  ASR ASR (.in_1(B), .in_2(A), .Result(ASR_result), .CarryOut(ASR_carryout));
  Sum Sum (.in_1(A), .in_2(B), .Result(Sum_result), .CarryOut(Sum_carryout));
  Difference Difference (.in_1(A), .in_2(B), .Result(Difference_result), .CarryOut(Difference_carryout));
  // Probe on ALUControl
  Multiplexer #(.select(4), .width(32), .enable("false")) multiplexer_1 (
    .in0(AND_result), .in1(OR_result), .in2(XOR_result), .in3(NOT_result), .in4(LSL_result),
    .in5(LSR_result), .in6(ASR_result), .in7(Sum_result), .in8(Difference_result), .out(Result),
    .sel(ALUControl));  // open: in9, in10, in11, in12, in13, in14, in15
  Multiplexer #(.select(4), .enable("false")) multiplexer_2 (
    .in0(AND_carryout), .in1(OR_carryout), .in2(XOR_carryout), .in3(NOT_carryout), .in4(LSL_carryout),
    .in5(LSR_carryout), .in6(ASR_carryout), .in7(Sum_carryout), .in8(Difference_carryout), .out(ALUFlags[1]),
    .sel(ALUControl));  // open: in9, in10, in11, in12, in13, in14, in15
  Comparator #(.width(32)) comparator_1 (.a({32{1'b0}}), .b(Result), .gt(ALUFlags[3]));  // open: eq, lt
  Comparator #(.width(32)) comparator_2 (.a({32{1'b0}}), .b(Result), .eq(ALUFlags[2]));  // open: gt, lt

  // Other names for the same wires on the sheet: oVerflow_t = ALUFlags[0]; Carry = ALUFlags[1];
  //   Overflow = ALUFlags[1]; Zero = ALUFlags[2]; Negative = ALUFlags[3]; Ctrl[3:0] = ALUControl

  // Notes on the sheet:
  //   INPUTS to your circuit
  //   DON'T CHANGE THE LOCATIONS OF THE INPUTS AND OUTPUTS!
  //   Result
  //   Carry
  //   OUTPUTS from your circuit
endmodule

module Sum (
  input  [31:0] in_1,
  input  [31:0] in_2,
  output [31:0] Result,
  output CarryOut
);

  Adder #(.width(32)) adder_1 (.a(in_1), .b(in_2), .out(Result), .cout(CarryOut));  // open: cin

  // Notes on the sheet:
  //   In1
  //   In2
endmodule

module Difference (
  input  [31:0] in_1,
  input  [31:0] in_2,
  output [31:0] Result,
  output CarryOut
);

  Subtractor #(.width(32)) subtractor_1 (.a(in_1), .b(in_2), .out(Result), .bout(CarryOut));  // open: bin

  // Notes on the sheet:
  //   In1
  //   In2
endmodule

module ASR (
  input  [31:0] in_1,
  input  [31:0] in_2,
  output [31:0] Result,
  output CarryOut
);

  wire [4:0] bitselector_1_out;

  BitSelector #(.width(32), .group(5)) bitselector_1 (.in(in_2), .out(bitselector_1_out), .sel(3'b000));
  Shifter #(.width(32), .shift("ar")) shifter_1 (.in(in_1), .\dist (bitselector_1_out), .out(Result));

  assign CarryOut = 1'b0;

  // Notes on the sheet:
  //   In1
  //   In2
endmodule

module LSL (
  input  [31:0] in_1,
  input  [31:0] in_2,
  output [31:0] Result,
  output CarryOut
);

  wire [4:0] bitselector_1_out;

  BitSelector #(.width(32), .group(5)) bitselector_1 (.in(in_2), .out(bitselector_1_out), .sel(3'b000));
  Shifter #(.width(32)) shifter_1 (.in(in_1), .\dist (bitselector_1_out), .out(Result));

  assign CarryOut = 1'b0;

  // Notes on the sheet:
  //   In1
  //   In2
endmodule

module LSR (
  input  [31:0] in_1,
  input  [31:0] in_2,
  output [31:0] Result,
  output CarryOut
);

  wire [4:0] bitselector_1_out;

  BitSelector #(.width(32), .group(5)) bitselector_1 (.in(in_2), .out(bitselector_1_out), .sel(3'b000));
  Shifter #(.width(32), .shift("lr")) shifter_1 (.in(in_1), .\dist (bitselector_1_out), .out(Result));

  assign CarryOut = 1'b0;

  // Notes on the sheet:
  //   In1
  //   In2
endmodule

module NOT (
  input  [31:0] in_1,
  output [31:0] Result,
  output CarryOut
);

  assign Result = ~in_1;  // NOT_Gate not_1, 32 bits wide

  assign CarryOut = 1'b0;

  // Notes on the sheet:
  //   In1
endmodule

module XOR (
  input  [31:0] in_1,
  input  [31:0] in_2,
  output [31:0] Result,
  output CarryOut
);

  assign Result = in_1 ^ in_2;  // XOR_Gate XOR, 32 bits wide

  assign CarryOut = 1'b0;

  // Notes on the sheet:
  //   In1
  //   In2
endmodule

module OR (
  input  [31:0] in_1,
  input  [31:0] in_2,
  output [31:0] Result,
  output CarryOut
);

  assign Result = in_1 | in_2;  // OR_Gate OR, 32 bits wide

  assign CarryOut = 1'b0;

  // Notes on the sheet:
  //   In1
  //   In2
endmodule

module AND (
  input  [31:0] in_1,
  input  [31:0] in_2,
  output [31:0] Result,
  output CarryOut
);

  assign Result = in_1 & in_2;  // AND_Gate AND, 32 bits wide

  assign CarryOut = 1'b0;

  // Notes on the sheet:
  //   In1
  //   In2
endmodule
